# Fritzing sketch MorseSketch (saved by Fritzing 0.9.3b)
breadboards: 1

parts:
  元件2 = Arduino Uno (Rev3)
  LED1 = LED - 5mm [color="Red (633nm)" package="5 mm [THT]"]
  R1 = Resistor [tolerance=±5% resistance=220 package=THT]
  S1 = Pushbutton [package="[THT]"]
  R2 = Resistor [tolerance=±5% resistance=220 package=THT]
  Grove1 = Grove OLED 128x96
  J1 = Piezo Speaker
  R3 = Resistor [tolerance=±5% resistance=220 package=THT]

nets:
  N1: 元件2.A4/SDA, Grove1.SDA
  N2: 元件2.A5/SCL, Grove1.SCL
  N3: 元件2.D12/MISO, R3.Pin_1
  N4: 元件2.D2, LED1.anode
  3V3: 元件2.3V3, Grove1.VCC
  N5: 元件2.5V, S1.Pin_3, S1.Pin_4
  GND: 元件2.GND, R1.Pin_0, R2.Pin_1, Grove1.GND, J1.pin1
  N6: LED1.cathode, R1.Pin_1
  N7: S1.Pin_1, S1.Pin_2, R2.Pin_0
  N8: J1.pin2, R3.Pin_0
